# Fritzing sketch DomoticShutter (saved by Fritzing 0.9.3b)
perfboards: 1

parts:
  U1 = RELAY-2 [package=relay-g5v]
  D1 = Diode [package=diode-1n4001]
  Q1 = NPN-Transistor [package="SOT-23 [SMD]"]
  Componente1 = Arduino Pro Mini (3.3V)
  U2 = RELAY-2 [package=relay-g5v]
  D2 = Diode [package=diode-1n4001]
  Q2 = NPN-Transistor [package="SOT-23 [SMD]"]
  U3 = RELAY-2 [package=relay-g5v]
  D3 = Diode [package=diode-1n4001]
  Q3 = NPN-Transistor [package="SOT-23 [SMD]"]
  U4 = RELAY-2 [package=relay-g5v]
  D4 = Diode [package=diode-1n4001]
  Q4 = NPN-Transistor [package="SOT-23 [SMD]"]
  U5 = RELAY-2 [package=relay-g5v]
  D5 = Diode [package=diode-1n4001]
  Q5 = NPN-Transistor [package="SOT-23 [SMD]"]
  U6 = RELAY-2 [package=relay-g5v]
  D6 = Diode [package=diode-1n4001]
  Q6 = NPN-Transistor [package="SOT-23 [SMD]"]
  Componente2 = FTDI Basic Programmer
  VCC1 = 4 x AAA Battery Mount
  S1 = Pushbutton [package=THT]
  S2 = Pushbutton [package=THT]
  S3 = Pushbutton [package=THT]
  S4 = Pushbutton [package=THT]

nets:
  N1: U1.2, D1.C, Componente1.RAW, U2.2, D2.C, U3.2, D3.C, U4.2, D4.C, U5.2, D5.C, U6.2, D6.C, VCC1.+
  N2: U1.9, D1.A, Q1.1
  GND: Q1.2, Componente1.GND, Q2.2, Q3.2, Q4.2, Q5.2, Q6.2, Componente2.CTS, Componente2.GND, VCC1.-, S1.leg0, S2.leg0, S3.leg0, S4.leg0
  N3: Q1.0, Componente1.D7
  N4: Componente1.DTR, Componente2.DTR
  N5: Componente1.TXO, Componente2.RXI
  N6: Componente1.RXI, Componente2.TXO
  N7: Componente1.VCC, Componente2.POWER
  N8: Componente1.MISO, Q6.0
  N9: Componente1.MOSI, Q5.0
  N10: Componente1.D10, Q4.0
  N11: Componente1.D9, Q3.0
  N12: Componente1.D8, Q2.0
  N13: Componente1.D6, S4.leg1
  N14: Componente1.D5, S3.leg1
  N15: Componente1.D4, S2.leg1
  N16: Componente1.D3, S1.leg1
  N17: U2.9, D2.A, Q2.1
  N18: U3.9, D3.A, Q3.1
  N19: U4.9, D4.A, Q4.1
  N20: U5.9, D5.A, Q5.1
  N21: U6.9, D6.A, Q6.1
